// Digital circuit slowbus_test.dig as structural Verilog
module slowbus_test (
  input  in_1,
  input  nOE,
  input  nSLOW,
  input  in_4,
  input  in_5,
  input  in_6,
  input  in_7,
  input  in_8
);

  wire CLK_out, undriven, undriven_2, undriven_3, undriven_4, undriven_5;

  Button CLK (.out(CLK_out));
  GAL16V8 gal16v8_1 ();
  LED led_1 (.in(undriven));
  LED Q0 (.in(undriven_2));
  LED Q1 (.in(undriven_3));
  LED Q2 (.in(undriven_4));
  LED PHO (.in(undriven_5));

  // Notes on the sheet:
  //   nSLOW: default 1
  //   =CLK/2 if /SLOW = 1
  //   =CLK/8 if /SLOW = 0
  //   contents of Fuses (hex, n*v repeats v):
  //   /home/anderson/src/m6502/gal/src/slowbus.hex false
endmodule
